// Logisim project LAB 11Integrate Instruction Fetch, Register File & ALU Modules.circ as structural Verilog: 5 circuits, main circuit main
module main (
  output [4:0] ReadReg1,
  output [4:0] ReadReg2,
  output [4:0] WriteReg,
  output [31:0] ReadData1,
  output Zero,
  output [31:0] ALU_Result,
  output [31:0] ReadData2
);

  wire Clock_out;
  wire [31:0] instructionfetchunit_1_ir;

  Clock Clock (.out(Clock_out));
  InstructionFetchUnit instructionfetchunit_1 (
    .Clock(Clock_out), .Enable(1'b1),
    .IR({instructionfetchunit_1_ir[31:26], ReadReg1, ReadReg2, WriteReg, instructionfetchunit_1_ir[10:0]}));
  RegisterFile registerfile_1 (
    .ReadReg1(ReadReg1), .ReadReg2(ReadReg2), .WriteReg(WriteReg), .WriteData(ALU_Result), .Clock(Clock_out),
    .Write(1'b1), .ReadData1(ReadData1), .ReadData2(ReadData2));
  ALU alu_1 (.Op1(ReadData1), .Op2(ReadData2), .ALUOp(3'b010), .Zero(Zero), .ALURes(ALU_Result));

  // Notes on the sheet:
  //   Enable
  //   The Instruction Fetch, Register File & ALU circuits integrated together in Main Canvas
  //   WriteData
  //   RegWrite
endmodule

// RegFile
module RegisterFile (
  input  Clock,
  input  [4:0] ReadReg1,
  input  [4:0] ReadReg2,
  input  [4:0] WriteReg,
  input  [31:0] WriteData,
  input  Write,
  output [31:0] ReadData1,
  output [31:0] ReadData2
);

  wire and_1_out, and_2_out, and_3_out, and_4_out, and_5_out, and_6_out, and_7_out, and_8_out, and_9_out,
       and_10_out, and_11_out, and_12_out, and_13_out, and_14_out, and_15_out, and_16_out, and_17_out,
       and_18_out, and_19_out, and_20_out, and_21_out, and_22_out, and_23_out, and_24_out, and_25_out,
       and_26_out, and_27_out, and_28_out, and_29_out, and_30_out, and_31_out, and_32_out, decoder_1_out0,
       decoder_1_out1, decoder_1_out2, decoder_1_out3, decoder_1_out4, decoder_1_out5, decoder_1_out6,
       decoder_1_out7, decoder_1_out8, decoder_1_out9, decoder_1_out10, decoder_1_out11, decoder_1_out12,
       decoder_1_out13, decoder_1_out14, decoder_1_out15, decoder_1_out16, decoder_1_out17, decoder_1_out18,
       decoder_1_out19, decoder_1_out20, decoder_1_out21, decoder_1_out22, decoder_1_out23, decoder_1_out24,
       decoder_1_out25, decoder_1_out26, decoder_1_out27, decoder_1_out28, decoder_1_out29, decoder_1_out30,
       decoder_1_out31;
  wire [31:0] _0_q, _1_q, _2_q, _3_q, _4_q, _5_q, _6_q, _7_q, _8_q, _9_q, _10_q, _11_q, _12_q, _13_q, _14_q,
       _15_q, _16_q, _17_q, _18_q, _19_q, _20_q, _21_q, _22_q, _23_q, _24_q, _25_q, _26_q, _27_q, _28_q,
       _29_q, _30_q, _31_q;

  Decoder #(.select(5), .enable("false")) decoder_1 (
    .out0(decoder_1_out0), .out1(decoder_1_out1), .out2(decoder_1_out2), .out3(decoder_1_out3),
    .out4(decoder_1_out4), .out5(decoder_1_out5), .out6(decoder_1_out6), .out7(decoder_1_out7),
    .out8(decoder_1_out8), .out9(decoder_1_out9), .out10(decoder_1_out10), .out11(decoder_1_out11),
    .out12(decoder_1_out12), .out13(decoder_1_out13), .out14(decoder_1_out14), .out15(decoder_1_out15),
    .out16(decoder_1_out16), .out17(decoder_1_out17), .out18(decoder_1_out18), .out19(decoder_1_out19),
    .out20(decoder_1_out20), .out21(decoder_1_out21), .out22(decoder_1_out22), .out23(decoder_1_out23),
    .out24(decoder_1_out24), .out25(decoder_1_out25), .out26(decoder_1_out26), .out27(decoder_1_out27),
    .out28(decoder_1_out28), .out29(decoder_1_out29), .out30(decoder_1_out30), .out31(decoder_1_out31),
    .sel(WriteReg));
  and and_1 (and_1_out, Write, decoder_1_out0);
  and and_2 (and_2_out, Write, decoder_1_out1);
  and and_3 (and_3_out, Write, decoder_1_out2);
  and and_4 (and_4_out, Write, decoder_1_out3);
  and and_5 (and_5_out, Write, decoder_1_out4);
  and and_6 (and_6_out, Write, decoder_1_out5);
  and and_7 (and_7_out, Write, decoder_1_out6);
  and and_8 (and_8_out, Write, decoder_1_out7);
  and and_9 (and_9_out, Write, decoder_1_out8);
  and and_10 (and_10_out, Write, decoder_1_out9);
  and and_11 (and_11_out, Write, decoder_1_out10);
  and and_12 (and_12_out, Write, decoder_1_out11);
  and and_13 (and_13_out, Write, decoder_1_out12);
  and and_14 (and_14_out, Write, decoder_1_out13);
  and and_15 (and_15_out, Write, decoder_1_out14);
  and and_16 (and_16_out, Write, decoder_1_out15);
  and and_17 (and_17_out, Write, decoder_1_out16);
  and and_18 (and_18_out, Write, decoder_1_out17);
  and and_19 (and_19_out, Write, decoder_1_out18);
  and and_20 (and_20_out, Write, decoder_1_out19);
  and and_21 (and_21_out, Write, decoder_1_out20);
  and and_22 (and_22_out, Write, decoder_1_out21);
  and and_23 (and_23_out, Write, decoder_1_out22);
  and and_24 (and_24_out, Write, decoder_1_out23);
  and and_25 (and_25_out, Write, decoder_1_out24);
  and and_26 (and_26_out, Write, decoder_1_out25);
  and and_27 (and_27_out, Write, decoder_1_out26);
  and and_28 (and_28_out, Write, decoder_1_out27);
  and and_29 (and_29_out, Write, decoder_1_out28);
  and and_30 (and_30_out, Write, decoder_1_out29);
  and and_31 (and_31_out, Write, decoder_1_out30);
  and and_32 (and_32_out, Write, decoder_1_out31);
  Register #(.width(32)) _0 (.D(WriteData), .en(and_1_out), .Q(_0_q), .clk(Clock));  // open: clr
  Register #(.width(32)) _1 (.D(WriteData), .en(and_2_out), .Q(_1_q), .clk(Clock));  // open: clr
  Register #(.width(32)) _2 (.D(WriteData), .en(and_3_out), .Q(_2_q), .clk(Clock));  // open: clr
  Register #(.width(32)) _3 (.D(WriteData), .en(and_4_out), .Q(_3_q), .clk(Clock));  // open: clr
  Register #(.width(32)) _4 (.D(WriteData), .en(and_5_out), .Q(_4_q), .clk(Clock));  // open: clr
  Register #(.width(32)) _5 (.D(WriteData), .en(and_6_out), .Q(_5_q), .clk(Clock));  // open: clr
  Register #(.width(32)) _6 (.D(WriteData), .en(and_7_out), .Q(_6_q), .clk(Clock));  // open: clr
  Register #(.width(32)) _7 (.D(WriteData), .en(and_8_out), .Q(_7_q), .clk(Clock));  // open: clr
  Register #(.width(32)) _8 (.D(WriteData), .en(and_9_out), .Q(_8_q), .clk(Clock));  // open: clr
  Register #(.width(32)) _9 (.D(WriteData), .en(and_10_out), .Q(_9_q), .clk(Clock));  // open: clr
  Register #(.width(32)) _10 (.D(WriteData), .en(and_11_out), .Q(_10_q), .clk(Clock));  // open: clr
  Register #(.width(32)) _11 (.D(WriteData), .en(and_12_out), .Q(_11_q), .clk(Clock));  // open: clr
  Register #(.width(32)) _12 (.D(WriteData), .en(and_13_out), .Q(_12_q), .clk(Clock));  // open: clr
  Register #(.width(32)) _13 (.D(WriteData), .en(and_14_out), .Q(_13_q), .clk(Clock));  // open: clr
  Register #(.width(32)) _14 (.D(WriteData), .en(and_15_out), .Q(_14_q), .clk(Clock));  // open: clr
  Register #(.width(32)) _15 (.D(WriteData), .en(and_16_out), .Q(_15_q), .clk(Clock));  // open: clr
  Register #(.width(32)) _16 (.D(WriteData), .en(and_17_out), .Q(_16_q), .clk(Clock));  // open: clr
  Register #(.width(32)) _17 (.D(WriteData), .en(and_18_out), .Q(_17_q), .clk(Clock));  // open: clr
  Register #(.width(32)) _18 (.D(WriteData), .en(and_19_out), .Q(_18_q), .clk(Clock));  // open: clr
  Register #(.width(32)) _19 (.D(WriteData), .en(and_20_out), .Q(_19_q), .clk(Clock));  // open: clr
  Register #(.width(32)) _20 (.D(WriteData), .en(and_21_out), .Q(_20_q), .clk(Clock));  // open: clr
  Register #(.width(32)) _21 (.D(WriteData), .en(and_22_out), .Q(_21_q), .clk(Clock));  // open: clr
  Register #(.width(32)) _22 (.D(WriteData), .en(and_23_out), .Q(_22_q), .clk(Clock));  // open: clr
  Register #(.width(32)) _23 (.D(WriteData), .en(and_24_out), .Q(_23_q), .clk(Clock));  // open: clr
  Register #(.width(32)) _24 (.D(WriteData), .en(and_25_out), .Q(_24_q), .clk(Clock));  // open: clr
  Register #(.width(32)) _25 (.D(WriteData), .en(and_26_out), .Q(_25_q), .clk(Clock));  // open: clr
  Register #(.width(32)) _26 (.D(WriteData), .en(and_27_out), .Q(_26_q), .clk(Clock));  // open: clr
  Register #(.width(32)) _27 (.D(WriteData), .en(and_28_out), .Q(_27_q), .clk(Clock));  // open: clr
  Register #(.width(32)) _28 (.D(WriteData), .en(and_29_out), .Q(_28_q), .clk(Clock));  // open: clr
  Register #(.width(32)) _29 (.D(WriteData), .en(and_30_out), .Q(_29_q), .clk(Clock));  // open: clr
  Register #(.width(32)) _30 (.D(WriteData), .en(and_31_out), .Q(_30_q), .clk(Clock));  // open: clr
  Register #(.width(32)) _31 (.D(WriteData), .en(and_32_out), .Q(_31_q), .clk(Clock));  // open: clr
  Multiplexer #(.select(5), .width(32), .enable("false")) multiplexer_1 (
    .in0(_0_q), .in1(_1_q), .in2(_2_q), .in3(_3_q), .in4(_4_q), .in5(_5_q), .in6(_6_q), .in7(_7_q),
    .in8(_8_q), .in9(_9_q), .in10(_10_q), .in11(_11_q), .in12(_12_q), .in13(_13_q), .in14(_14_q),
    .in15(_15_q), .in16(_16_q), .in17(_17_q), .in18(_18_q), .in19(_19_q), .in20(_20_q), .in21(_21_q),
    .in22(_22_q), .in23(_23_q), .in24(_24_q), .in25(_25_q), .in26(_26_q), .in27(_27_q), .in28(_28_q),
    .in29(_29_q), .in30(_30_q), .in31(_31_q), .out(ReadData1), .sel(ReadReg1));
  Multiplexer #(.select(5), .width(32), .enable("false")) multiplexer_2 (
    .in0(_0_q), .in1(_1_q), .in2(_2_q), .in3(_3_q), .in4(_4_q), .in5(_5_q), .in6(_6_q), .in7(_7_q),
    .in8(_8_q), .in9(_9_q), .in10(_10_q), .in11(_11_q), .in12(_12_q), .in13(_13_q), .in14(_14_q),
    .in15(_15_q), .in16(_16_q), .in17(_17_q), .in18(_18_q), .in19(_19_q), .in20(_20_q), .in21(_21_q),
    .in22(_22_q), .in23(_23_q), .in24(_24_q), .in25(_25_q), .in26(_26_q), .in27(_27_q), .in28(_28_q),
    .in29(_29_q), .in30(_30_q), .in31(_31_q), .out(ReadData2), .sel(ReadReg2));
endmodule

// IF
module InstructionFetchUnit (
  input  Clock,
  input  Enable,
  output [31:0] IR
);

  wire [31:0] adder_1_out, register_1_q;

  Register #(.width(32)) register_1 (.D(adder_1_out), .Q(register_1_q), .clk(Clock));  // open: en, clr
  Adder #(.width(32)) adder_1 (.a(register_1_q), .b(32'h1), .out(adder_1_out));  // open: cin, cout
  RAM #(.addrWidth(24), .dataWidth(32)) ram_1 (
    .addr(register_1_q[23:0]), .data(IR), .clk(Clock), .ld(Enable));  // open: sel, clr

  // Notes on the sheet:
  //   PC
  //   Instrucion Memory
endmodule

module ALU (
  input  [31:0] Op1,
  input  [31:0] Op2,
  input  [2:0] ALUOp,
  output Zero,
  output [31:0] ALURes
);

  wire [31:0] adder_1_out, adder_2_out, and_1_out, bit_extender_1_out, not_1_out, or_1_out;

  assign and_1_out = Op1 & Op2;  // AND_Gate and_1, 32 bits wide
  assign or_1_out = Op1 | Op2;  // OR_Gate or_1, 32 bits wide
  Adder #(.width(32)) adder_1 (.a(Op1), .b(Op2), .out(adder_1_out));  // open: cin, cout
  Adder #(.width(32)) adder_2 (.a(Op1), .b(not_1_out), .out(adder_2_out), .cin(1'b1));  // open: cout
  assign not_1_out = ~Op2;  // NOT_Gate not_1, 32 bits wide
  assign bit_extender_1_out = {{31{1'b0}}, adder_2_out[31]};  // Bit_Extender bit_extender_1
  Multiplexer #(.select(3), .width(32), .enable("false")) multiplexer_1 (
    .in0(and_1_out), .in1(or_1_out), .in2(adder_1_out), .in6(adder_2_out), .in7(bit_extender_1_out),
    .out(ALURes), .sel(ALUOp));  // open: in3, in4, in5
  Comparator #(.width(32)) comparator_1 (.a({32{1'b0}}), .b(ALURes), .eq(Zero));  // open: gt, lt
endmodule

module second_main (
  output [31:0] ReadData1,
  output Zero,
  output [31:0] ReadData2,
  output [31:0] ALU_Result
);

  wire Clock_out;
  wire [31:0] instructionfetchunit_1_ir;

  Clock Clock (.out(Clock_out));
  InstructionFetchUnit instructionfetchunit_1 (.Clock(Clock_out), .Enable(1'b1), .IR(instructionfetchunit_1_ir));
  Register #(.width(32)) register_1 (.D(instructionfetchunit_1_ir), .clk(Clock_out));  // open: en, Q, clr
  RegisterFile registerfile_1 (
    .ReadReg1(5'b00001), .ReadReg2(5'b00010), .WriteReg(5'b00010), .WriteData(32'h5), .Clock(Clock_out),
    .Write(1'b1), .ReadData1(ReadData1), .ReadData2(ReadData2));
  ALU alu_1 (.Op1(ReadData1), .Op2(ReadData2), .ALUOp(3'b111), .Zero(Zero), .ALURes(ALU_Result));

  // Notes on the sheet:
  //   Enable
  //   IR
  //   ReadReg1
  //   ReadReg2
  //   WriteReg
  //   WriteData
  //   RegWrite
endmodule
